# Fritzing sketch SPCT Light Panel High Level (saved by Fritzing 0.9.3b)
breadboards: 1

parts:
  Communication_Hub = Raspberry Pi Zero
  Light_Controller = Arduino Uno (Rev3)
  Light_Bank_2 = Neopixel Strip -- White (30/m)
  Light_Bank_1 = Neopixel Strip -- White (30/m)
  Light_Bank_0 = Neopixel Strip -- White (30/m)
  C1 = Capacitor Polarized [package=cpol-radial-1000uf-25v]
  C2 = Capacitor Polarized [package=cpol-radial-1000uf-25v]
  C3 = Capacitor Polarized [package=cpol-radial-1000uf-25v]
  J1 = Power Jack [package=power_jack_pth]
  R1 = Resistor [tolerance=±5% resistance=1k package=THT]
  Part1 = Adafruit 4-channel I2C-safe Bi-directional Logic Level Converter [part_number="Adafruit #757"]

nets:
  N1: Communication_Hub.pin_1, Communication_Hub.pin_17, Part1.LV
  N2: Communication_Hub.pin_2, Communication_Hub.pin_4, R1.Pin_0
  GND: Communication_Hub.pin_6, Communication_Hub.pin_25, Communication_Hub.pin_34, Communication_Hub.pin_39, Light_Controller.GND, Light_Bank_2.GND, Light_Bank_1.GND, Light_Bank_0.GND, C1.-, C2.-, C3.-, J1.GND, Part1.GND
  N3: Communication_Hub.pin_8, Part1.A2
  N4: Communication_Hub.pin_10, Part1.A1
  N5: Light_Controller.D9_PWM, Light_Bank_0.Din
  N6: Light_Controller.D10_PWM/SS, Light_Bank_1.Din
  N7: Light_Controller.D11_PWM/MOSI, Light_Bank_2.Din
  N8: Light_Controller.D0/RX, Part1.B2
  N9: Light_Controller.D1/TX, Part1.B1
  +5V: Light_Controller.VIN, Light_Bank_2.+5V, Light_Bank_1.+5V, Light_Bank_0.+5V, C1.+, C2.+, C3.+, J1.PWR, R1.Pin_1, Part1.HV

custom parts:
  Neopixel Strip -- White (30/m): These NeoPixel strips have 30 digitally-addressable pixel LEDs per meter and are very affordable and are only 12.5 mm wide, 10 mm if you remove the strip from the casing.
  Adafruit 4-channel I2C-safe Bi-directional Logic Level Converter: Because the Arduino (and Basic Stamp) are 5V devices, and most modern sensors, displays, flash cards and modes are 3.3V-only, many makers find that they need to perform level shifting/conversion to protect the 3.3V device from 5V. We do have some other handy level shifters in the shop, from the DIP 74LVC245 to the fancy bi-directional TXB0108. However, neither of these are happy to work with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
